# Fritzing sketch TinyTony-fritzing (saved by Fritzing 0.9.3b)
breadboards: 1

parts:
  U1 = attiny85 [package=dip]
  C1 = Ceramic Capacitor [capacitance=100nF package="100 mil [THT, multilayer]"]
  C2 = Ceramic Capacitor [capacitance=100nF package="100 mil [THT, multilayer]"]
  IR1 = TSOP312.., 314.. [package=THT]
  IC1 = IC, DIP package, 10 pins [chip_label=DRV]
  IC2 = IC, DIP package, 10 pins [chip_label=DRV]
  M1 = DC Motor
  M2 = DC Motor
  R2 = Resistor [tolerance=±5% resistance=1k package=THT]
  R1 = Resistor [tolerance=±5% resistance=1k package=THT]
  U2 = LIPO-1000mAh [package=lipo-1000]
  R3 = Photocell (LDR) [package=THT]
  R4 = Photocell (LDR) [package=THT]

nets:
  N1: U1.Pin_2, R3.pin_1, R4.pin_0
  N2: U1.Pin_3, IR1.GND
  N3: U1.Pin_4, C2.1, IC1.pin5, R4.pin_1
  N4: U1.Pin_5, IC1.pin9, IC2.pin9, R2.Pin_1
  N5: U1.Pin_7, IC1.pin10, IC2.pin10, R1.Pin_1
  N6: U1.Pin_8, C1.0, IR1.Data, IC2.pin4, R2.Pin_0, R1.Pin_0, U2.+
  N7: C1.1, IR1.Vs, IC2.pin5, U2.-
  N8: C2.0, IC1.pin4, R3.pin_0
  N9: IC1.pin1, M1.pin_2
  N10: IC1.pin3, M1.pin_1
  N11: IC2.pin1, M2.pin_2
  N12: IC2.pin3, M2.pin_1
